# Fritzing sketch electronics_sketch (saved by Fritzing 0.9.3b)
breadboards: 1

parts:
  Part1 = Arduino Uno (Rev3)
  Part2 = adafruit [part_number="Adafruit #1334"]
  LCD1 = LCD screen
  R1 = TRIMPOT [package=3386u]
  S1 = Pushbutton [package="[SMD]"]
  S2 = Pushbutton [package="[SMD]"]

nets:
  N1: Part1.A4/SDA, Part2.connector12
  N2: Part1.A5/SCL, Part2.connector11
  N3: Part1.D11_PWM/MOSI, S1.Pin_3, S1.Pin_4
  N4: Part1.D12/MISO, S2.Pin_3, S2.Pin_4
  N5: Part1.D0/RX, LCD1.LED-
  N6: Part1.D1/TX, LCD1.LED+
  N7: Part1.D2, LCD1.DB7
  N8: Part1.D3_PWM, LCD1.DB6
  N9: Part1.D4, LCD1.DB5
  N10: Part1.D5_PWM, LCD1.DB4
  N11: Part1.D6_PWM, LCD1.E
  N12: Part1.D7, LCD1.RS
  N13: Part2.connector13, Part2.connector14
  N14: LCD1.V0, R1.WIPER
